// Logisim project alu2.circ as structural Verilog: 3 circuits, main circuit main
module main (
  input  [3:0] FunSel,
  input  [7:0] A,
  input  [7:0] B,
  output [7:0] Out
);

  wire undriven_2;
  wire [7:0] and_1_out, arithmetic_unit_1_out, nor_1_out, not_1_out, not_2_out, or_1_out, undriven;

  arithmetic_unit arithmetic_unit_1 (.FunSel(FunSel[1:0]), .A(A), .B(B), .Out(arithmetic_unit_1_out));  // open: Carry
  assign and_1_out = A & B;  // AND_Gate and_1, 8 bits wide
  assign or_1_out = A | B;  // OR_Gate or_1, 8 bits wide
  assign nor_1_out = ~(A | B);  // NOR_Gate nor_1, 8 bits wide
  shifter shifter_1 (.Out(undriven), .CarryOut(undriven_2), .Funsel(FunSel[2:0]), .A(A));  // open: in_5, in_3, in_6
  assign not_1_out = ~A;  // NOT_Gate not_1, 8 bits wide
  assign not_2_out = ~A;  // NOT_Gate not_2, 8 bits wide
  Multiplexer #(.select(4), .width(8)) multiplexer_1 (
    .in0(A), .in1(B), .in2(not_1_out), .in3(not_2_out), .in4(arithmetic_unit_1_out),
    .in5(arithmetic_unit_1_out), .in6(arithmetic_unit_1_out), .in7(and_1_out), .in8(or_1_out),
    .in9(nor_1_out), .in10(undriven), .in11(undriven), .in12(undriven), .in13(undriven), .in14(undriven),
    .in15(undriven), .out(Out), .sel(FunSel));  // open: en

  // Notes on the sheet:
  //   Carry register will come here
endmodule

// Arithmetic Unit
module arithmetic_unit (
  input  [1:0] FunSel,
  input  [7:0] A,
  input  [7:0] B,
  input  Carry,
  output [7:0] Out
);

  wire and_1_out, undriven;
  wire [7:0] adder_1_out, subtractor_1_out;

  and and_1 (and_1_out, undriven, FunSel[0]);
  Adder adder_1 (.a(A), .b(B), .out(adder_1_out), .cin(and_1_out));  // open: cout
  Subtractor subtractor_1 (.a(A), .b(B), .out(subtractor_1_out));  // open: bin, bout
  Multiplexer #(.select(2), .width(8)) multiplexer_1 (
    .in0(adder_1_out), .in1(adder_1_out), .in2(subtractor_1_out), .in3(subtractor_1_out), .out(Out),
    .sel(FunSel));  // open: en
endmodule

module shifter (
  input  [2:0] Funsel,
  input  [7:0] A,
  input  in_3,
  input  [7:0] Out,
  input  in_5,
  input  in_6,
  input  CarryOut
);

  Multiplexer #(.select(3), .width(8), .enable("false")) multiplexer_1 (
    .in0({A[6:0], in_3}), .in1({A[6:0], in_3}), .in2({A[6:0], in_3}), .in3({in_5, A[7:1]}),
    .in4({A[6:0], in_6}), .in5({{2{A[7]}}, A[6:1]}), .in6({A[6:0], A[7]}), .in7({A[0], A[7:1]}), .out(Out),
    .sel(Funsel));
  Multiplexer #(.select(3), .enable("false")) multiplexer_2 (
    .in0(A[7]), .in1(A[7]), .in2(A[7]), .in3(A[0]), .in4(A[7]), .in5(A[7]), .in6(A[7]), .in7(A[0]),
    .out(CarryOut), .sel(Funsel));

  // Notes on the sheet:
  //   Carry
endmodule
